# Fritzing sketch 1602-Mega (saved by Fritzing 0.9.2b)

parts:
  Part1 = DeuLigne 1.1 - The Snootlab's LCD shield for Arduino
  Part2 = Arduino Mega 2560 (Rev3)

nets:
  N1: Part1.RESET, Part2.RESET
  +5V: Part1.+5V, Part2.5V
  GND: Part1.GND, Part2.GND
  N2: Part1.A0, Part2.A0
  N3: Part1.D8, Part2.D8_PWM
  N4: Part1.D9, Part2.D9_PWM
  N5: Part1.D10_SS, Part2.D10_PWM
  N6: Part1.D4, Part2.D4_PWM
  N7: Part1.D5, Part2.D5_PWM
  N8: Part1.D6, Part2.D6_PWM
  N9: Part1.D7, Part2.D7_PWM
