# Fritzing sketch AccBoard (saved by Fritzing 0.9.3b)
perfboards: 1

parts:
  Part1 = DeuLigne 1.1 - The Snootlab's LCD shield for Arduino
  U3 = SWITCH_SPDT [package=kps-1290]
  Pololu_A1 = Pololu A4988 [package=SO16]
  Power_plug1 = Power plug
  F4 = Resettable Fuse PTC [package=ptc]
  LED1 = LED - 5mm [color="Red (633nm)" package="5 mm [THT]"]
  C1 = Electrolytic Capacitor [capacitance=10µF voltage=50V package="100 mil [THT, electrolytic]"]
  J4 = male pin header, 3 pins [form="♂ (male)"]
  J2 = male pin header, 2 pins [form="♂ (male)"]
  J5 = male pin header, 3 pins [form="♂ (male)"]
  R1 = Resistor [tolerance=±5% resistance=220 package=THT]
  J6 = male pin header, 3 pins [form="♂ (male)"]
  J7 = male pin header, 3 pins [form="♂ (male)"]
  J8 = male pin header, 3 pins [form="♂ (male)"]
  J9 = male pin header, 4 pins [form="♂ (male)"]
  J10 = male pin header, 4 pins [form="♂ (male)"]
  C2 = Ceramic Capacitor [capacitance=100nF package="100 mil [THT, multilayer]"]  # not connected
  C3 = Electrolytic Capacitor [capacitance=1µF package="100 mil [THT, electrolytic]"]
  S1 = Tilt Switch [package=THT]
  J11 = Basic Servo
  Part2 = Arduino Mega 2560 (Rev3)
  U4 = RELAY [package=relay-g5q]
  Part3 = Real Time Clock Module - DS1307 RTC Breakout Board
  LED2 = LED - 5mm [color="Red (633nm)" package="5 mm [THT]"]
  LED3 = LED - 5mm [color="Red (633nm)" package="5 mm [THT]"]
  J13 = male pin header, 2 pins [form="♂ (male)"]
  J12 = female pin header, 6 pins [form="♀ (female)"]
  Part4 = NRF24L01+ Breakout Board
  Part5 = Arduino Uno (Rev3)
  Part6 = NRF24L01+ Breakout Board
  JP1 = FTDI_BASIC [package=ftdi_basic]  # not connected
  Part7 = DeuLigne 1.1 - The Snootlab's LCD shield for Arduino

nets:
  +3V3: Part1.+3V3, Part4.VCC
  GND: Part1.GND, Part4.GND, Part6.GND, Part7.GND
  N1: U3.O, Pololu_A1.DIR, LED1.anode, J2.pin2
  N2: Pololu_A1.ENABLE, C1.-, J4.pin1
  N3: Pololu_A1.GND#8, Power_plug1.GND, F4.1, LED1.cathode, J2.pin1
  N4: Pololu_A1.VMOT, C1.+, J5.pin1, J10.pin4, C3.-, Part2.GND
  N5: Power_plug1.VCC, F4.2
  N6: J4.pin3, J6.pin1, LED3.anode
  N7: J5.pin3, J7.pin1
  N8: R1.Pin_0, J8.pin1, LED3.cathode
  N9: J6.pin2, S1.Pin_1, LED2.anode
  N10: J6.pin3, J9.pin4
  N11: J7.pin2, S1.Pin_2
  N12: J8.pin2, LED2.cathode
  N13: J8.pin3, Part2.A15
  N14: J9.pin1, C3.+
  N15: J9.pin3, J11.vcc
  N16: J10.pin2, J11.gnd
  N17: J11.pulse, Part2.D26
  N18: Part2.D21/SCL, J13.pin2
  N19: Part2.D20/SDA, J13.pin1
  N20: Part2.D53, U4.MAIN
  N21: Part3.5V, J12.pin6
  N22: Part3.GND, J12.pin5
  N23: Part3.SCL, J12.pin4
  N24: Part3.SDA, J12.pin3
  3V3: Part5.3V3, Part6.VCC

notes:
  Fuse, switch, light
  12v 2a
  float switches
  doser / pump Relay
  pin 53
  float switch
  pin A15
  feeder servo
  pin 30-34
  doser
  pin 26
  RTC 3231
  PH Sensor
  v+, G, G, Po, Do, To
  IC2 arduino to arduino comm
  SDA, SCL, GRD
