# Fritzing sketch AquariumController (saved by Fritzing 0.9.3b)
perfboards: 1

parts:
  J11 = Basic Servo
  HLK-PM1 = HLK-PM01
  Part8 = Soil Moisture Sensor
  U5 = 4-Channel 5v Relay Shield [package=relay-4ch5v10a]
  VALVE1 = Plastic Solenoid Valve
  Part9 = 16-Channel 12-bit PWM Servo Driver - I2C [part_number=815]
  HLK-PM3 = HLK-PM01  # not connected
  M1 = DC Motor
  M2 = DC Motor
  J14 = male pin header, 2 pins [form="♂ (male)"]
  F5 = Resettable Fuse PTC [package=ptc]
  Pololu_A2 = Pololu A4988 [package=SO16]
  LED4 = LED - 5mm [color="Red (633nm)" package="5 mm [THT]"]
  U6 = SWITCH_SPDT [package=kps-1290]
  Power_plug3 = Power plug
  C5 = Electrolytic Capacitor [capacitance=10µF voltage=50V package="100 mil [THT, electrolytic]"]
  J15 = male pin header, 3 pins [form="♂ (male)"]
  J16 = male pin header, 3 pins [form="♂ (male)"]  # not connected
  R3 = Resistor [tolerance=±5% resistance=220 package=THT]
  J17 = male pin header, 4 pins [form="♂ (male)"]
  J19 = male pin header, 3 pins [form="♂ (male)"]  # not connected
  J20 = male pin header, 3 pins [form="♂ (male)"]  # not connected
  J21 = male pin header, 3 pins [form="♂ (male)"]
  S2 = Tilt Switch [package=THT]
  Part10 = Real Time Clock Module - DS1307 RTC Breakout Board
  LED5 = LED - 5mm [color="Red (633nm)" package="5 mm [THT]"]
  LED6 = LED - 5mm [color="Red (633nm)" package="5 mm [THT]"]
  J26 = male pin header, 4 pins [form="♂ (male)"]  # not connected
  J27 = male pin header, 4 pins [form="♂ (male)"]
  J25 = male pin header, 12 pins [form="♂ (male)"]
  J24 = male pin header, 12 pins [form="♂ (male)"]
  J28 = male pin header, 4 pins [form="♂ (male)"]  # not connected
  J29 = male pin header, 4 pins [form="♂ (male)"]  # not connected
  J30 = male pin header, 4 pins [form="♂ (male)"]  # not connected
  LED7 = LED - 5mm [color="Red (633nm)" package="5 mm [THT]"]  # not connected
  R4 = Resistor [tolerance=±5% resistance=220 package=THT]
  R5 = Resistor [tolerance=±5% resistance=220 package=THT]
  LED8 = LED - 5mm [color="Red (633nm)" package="5 mm [THT]"]
  J31 = male pin header, 8 pins [form="♂ (male)"]
  J32 = male pin header, 8 pins [form="♂ (male)"]
  J33 = male pin header, 2 pins [form="♂ (male)"]
  J35 = male pin header, 2 pins [form="♂ (male)"]
  Part11 = Arduino Uno (Rev3)  # not connected
  Part12 = Arduino Mega 2560 (Rev3)
  R6 = Resistor [tolerance=±5% resistance=220 package=THT]
  C6 = Ceramic Capacitor [capacitance=100nF package="100 mil [THT, multilayer]"]
  HLK-PM5 = HLK-PM01  # not connected
  JP3 = FTDI_BASIC [package=ftdi_basic]  # not connected
  Part13 = DeuLigne 1.1 - The Snootlab's LCD shield for Arduino
  Part14 = DeuLigne 1.1 - The Snootlab's LCD shield for Arduino
  Power_plug4 = Power plug  # not connected

nets:
  GND: J11.gnd, Part9.GND, J25.pin9, J31.pin4
  N1: J11.vcc, Part9.5.0V
  N2: J11.pulse, Part9.PWM0
  N3: HLK-PM1.-Vo, M1.pin_2
  N4: HLK-PM1.+Vo, U5.K3-On
  N5: Part8.SIG, J35.pin2
  N6: Part8.GND, R5.Pin_0, LED8.cathode, J31.pin7
  N7: Part8.VCC, J32.pin7
  N8: U5.VCC, J32.pin5
  N9: U5.GND, J31.pin3
  N10: U5.IN1, Part9.PWM5
  N11: U5.IN2, Part9.PWM6
  N12: U5.K1-Off, M2.pin_1
  N13: U5.K1-On, U5.K2-On
  N14: U5.K2-Off, VALVE1.no_name_yet#1
  N15: U5.K3-Off, M1.pin_1
  N16: U5.IN3, Part9.PWM7
  N17: VALVE1.no_name_yet#2, M2.pin_2
  N18: Part9.PWRIN, J32.pin4
  N19: Part9.VCC, J24.pin9
  N20: Part9.SDA, J17.pin1
  N21: Part9.SCL, J27.pin1
  N22: J14.pin2, Pololu_A2.DIR, LED4.anode, U6.O, J25.pin10
  N23: F5.2, Power_plug3.VCC
  N24: Pololu_A2.ENABLE, C5.-, J15.pin1
  N25: Pololu_A2.VMOT, Part12.GND
  N26: LED4.cathode, J24.pin3
  N27: J15.pin3, J21.pin1, LED5.anode
  N28: R3.Pin_1, S2.Pin_1, LED6.anode, J32.pin1
  N29: J17.pin3, Part10.SDA
  N30: S2.Pin_2, J31.pin1
  N31: Part10.5V, J24.pin11
  N32: Part10.GND, J25.pin11
  N33: Part10.SCL, J27.pin3
  N34: LED6.cathode, J33.pin1, Part12.A13
  N35: R4.Pin_1, J32.pin2
  N36: R5.Pin_1, LED8.anode, J35.pin1, Part12.A14
  N37: R6.Pin_0, C6.0
  GND_2: R6.Pin_1, Part13.GND, Part14.GND
  N38: C6.1, Part13.A5(CLK)

notes:
  Tank pump Relay,
  12v 2a, pin 37
  24v 6a psu
  RO pump Relay,
  24v 6a, pin 36
  12v 20a psu
  water level sensor (overflow)
  5v20ma, pin ??
  water solenoid valve
  12v 500ma, pin ??
  Fuse, switch, light
  float switche
  12v 20a
  RTC 3231
  5v 6a servo pwm
  RO valve Relay,
  12v 500ma
  Arduino 5v rail
  5v
  SDA
  SLC
  TX
  RX
  Grd
  IC2 arduino to arduino comm
  SDA, SCL, GRD
  low pass filter
  100K Res, 10 uf Cap
  PH Sensor
  v+, G, G, Po, Do, To
  float switch
  pin A15
  9v 1a psu
  9v 1a

custom parts:
  4-Channel 5v Relay Shield: 4 Channel 5v Relay Shield w. 2x SPD-06VDC-SD-C
  16-Channel 12-bit PWM Servo Driver - I2C: You want to make a cool robot, maybe a hexapod walker, or maybe just a piece of art with a lot of moving parts. Or maybe you want to drive a lot of LEDs with precise PWM output. Using only two pins, control 16 free-running PWM outputs! You can even chain up 62 breakouts to control up to 992 PWM outputs.
