# Fritzing sketch LeoISP (saved by Fritzing 0.9.2b)

parts:
  Part1 = Arduino Uno (Rev3)
  Part2 = Arduino Leonardo (Rev3b)  # not connected
  C1 = Electrolytic Capacitor [capacitance=10µF package="100 mil [THT, electrolytic]"]

nets:
  N1: Part1.RESET, C1.-
  N2: Part1.GND, C1.+

notes:
  10 uF Capacitor
  To PC
